// Logisim project Combinational_Circuits.circ as structural Verilog: 1 circuit, main circuit main
module main (
  input  X,
  input  Y,
  input  Z
);

  wire and_1_out, and_2_out, and_3_out, and_4_out, not_1_out, not_2_out, not_3_out, or_1_out, or_2_out,
       or_3_out, or_4_out, or_5_out, or_6_out;

  not not_1 (not_1_out, X);
  not not_2 (not_2_out, Y);
  not not_3 (not_3_out, Z);
  and and_1 (and_1_out, not_1_out, not_2_out, Z);
  and and_2 (and_2_out, not_1_out, Y, not_3_out);
  and and_3 (and_3_out, not_1_out, Y, Z);
  and and_4 (and_4_out, X, not_2_out, not_3_out);
  or or_1 (or_1_out, and_1_out, and_2_out, and_3_out, and_4_out);
  or or_2 (or_2_out, and_1_out, and_3_out, and_4_out);
  or or_3 (or_3_out, and_2_out, and_3_out);
  buf or_4 (or_4_out, and_4_out);  // OR_Gate
  or or_5 (or_5_out, and_2_out, and_3_out, and_4_out);
  buf or_6 (or_6_out, and_2_out);  // OR_Gate
  _7_Segment_Display u_7_segment_display_1 (
    .g(or_5_out), .f(or_4_out), .a(or_3_out), .b(or_1_out), .e(or_6_out), .d(or_3_out), .c(or_2_out));  // open: dp
endmodule
