// Logisim project Die_Circuit_Problem.circ as structural Verilog: 1 circuit, main circuit main
module main (
  input  x___2_0,
  input  y___2_1,
  input  z__2_2
);

  wire and_1_out, and_2_out, and_3_out, and_4_out, and_5_out, and_6_out, and_7_out, and_8_out, and_9_out,
       and_10_out, not_1_out, not_2_out, not_3_out, or_1_out, or_2_out, or_3_out, or_4_out;

  not not_1 (not_1_out, x___2_0);
  not not_2 (not_2_out, y___2_1);
  not not_3 (not_3_out, z__2_2);
  and and_1 (and_1_out, x___2_0, y___2_1, not_3_out);
  and and_2 (and_2_out, x___2_0, not_2_out, not_3_out);
  and and_3 (and_3_out, y___2_1, not_1_out, not_3_out);
  and and_4 (and_4_out, not_1_out, not_2_out, z__2_2);
  and and_5 (and_5_out, and_1_out, y___2_1);
  and and_6 (and_6_out, and_2_out, and_3_out);
  and and_7 (and_7_out, and_2_out, and_4_out);
  and and_8 (and_8_out, not_2_out, z__2_2, x___2_0);
  or or_1 (or_1_out, and_2_out, and_5_out, and_8_out, and_6_out);
  or or_2 (or_2_out, and_6_out, and_5_out, or_3_out, and_8_out, and_3_out);
  or or_3 (or_3_out, and_7_out, and_8_out, and_9_out, and_4_out);
  and and_9 (and_9_out, not_1_out, y___2_1, z__2_2);
  and and_10 (and_10_out, or_2_out, or_4_out);
  or or_4 (or_4_out, and_7_out, and_9_out);
  LED led_1 (.in(or_2_out));
  LED led_2 (.in(and_10_out));
  LED led_3 (.in(or_3_out));
  LED led_4 (.in(or_1_out));
  LED led_5 (.in(or_3_out));
  LED led_6 (.in(and_10_out));
  LED led_7 (.in(or_2_out));
endmodule
